// Logisim project logicfinal.circ as structural Verilog: 1 circuit, main circuit main
module main (
);

  wire and_1_out, button_1_out, button_2_out, n7447_1_pin9, n7447_1_pin10, n7447_1_pin11, n7447_1_pin12,
       n7447_1_pin13, n7447_1_pin14, n7447_1_pin15, n7447_2_pin9, n7447_2_pin10, n7447_2_pin11,
       n7447_2_pin12, n7447_2_pin13, n7447_2_pin14, n7447_2_pin15, n74161_1_pin3, n74161_1_pin7,
       n74161_1_pin11, n74161_1_pin12, n74161_1_pin13, n74161_1_pin14, n74161_2_pin2, n74161_2_pin3,
       n74161_2_pin7, n74161_2_pin11, n74161_2_pin12, n74161_2_pin13, n74161_2_pin14, not_1_out, not_2_out;

  not not_1 (not_1_out, button_1_out);
  Button button_1 (.out(button_1_out));
  and and_1 (and_1_out, not_1_out, not_2_out);
  Button button_2 (.out(button_2_out));
  not not_2 (not_2_out, n74161_2_pin2);
  _74161 #(.ShowInternalStructure("true")) u_74161_1 (
    .pin1(and_1_out), .pin2(button_2_out), .pin3(n74161_1_pin3), .pin4(n74161_1_pin3), .pin5(n74161_1_pin3),
    .pin6(n74161_1_pin3), .pin7(n74161_1_pin7), .pin14(n74161_1_pin14), .pin13(n74161_1_pin13),
    .pin12(n74161_1_pin12), .pin11(n74161_1_pin11), .pin10(n74161_1_pin7), .pin9(n74161_1_pin7));  // open: pin15
  _74161 #(.ShowInternalStructure("true")) u_74161_2 (
    .pin1(not_1_out), .pin2(n74161_2_pin2), .pin3(n74161_2_pin3), .pin4(n74161_2_pin3), .pin5(n74161_2_pin3),
    .pin6(n74161_2_pin3), .pin7(n74161_2_pin7), .pin14(n74161_2_pin14), .pin13(n74161_2_pin13),
    .pin12(n74161_2_pin12), .pin11(n74161_2_pin11), .pin10(n74161_2_pin7), .pin9(n74161_2_pin7));  // open: pin15
  and and_2 (n74161_2_pin2, n74161_1_pin13, n74161_1_pin11);
  _7447 #(.ShowInternalStructure("true")) u_7447_1 (
    .pin1(n74161_1_pin13), .pin2(n74161_1_pin12), .pin6(n74161_1_pin11), .pin7(n74161_1_pin14),
    .pin15(n7447_1_pin15), .pin14(n7447_1_pin14), .pin13(n7447_1_pin13), .pin12(n7447_1_pin12),
    .pin11(n7447_1_pin11), .pin10(n7447_1_pin10), .pin9(n7447_1_pin9));  // open: pin3, pin4, pin5
  _7447 #(.ShowInternalStructure("true")) u_7447_2 (
    .pin1(n74161_2_pin13), .pin2(n74161_2_pin12), .pin6(n74161_2_pin11), .pin7(n74161_2_pin14),
    .pin15(n7447_2_pin15), .pin14(n7447_2_pin14), .pin13(n7447_2_pin13), .pin12(n7447_2_pin12),
    .pin11(n7447_2_pin11), .pin10(n7447_2_pin10), .pin9(n7447_2_pin9));  // open: pin3, pin4, pin5
  _7_Segment_Display #(.active("false"), .decimalPoint("false")) u_7_segment_display_1 (
    .g(n7447_2_pin14), .f(n7447_2_pin15), .a(n7447_2_pin13), .b(n7447_2_pin12), .e(n7447_2_pin9),
    .d(n7447_2_pin10), .c(n7447_2_pin11));
  _7_Segment_Display #(.active("false"), .decimalPoint("false")) u_7_segment_display_2 (
    .g(n7447_1_pin14), .f(n7447_1_pin15), .a(n7447_1_pin13), .b(n7447_1_pin12), .e(n7447_1_pin9),
    .d(n7447_1_pin10), .c(n7447_1_pin11));
  // also tied to GND on the sheet: {n74161_1_pin3, n74161_2_pin3}
  // also tied to VCC on the sheet: {n74161_1_pin7, n74161_2_pin7}
endmodule
